# Fritzing sketch DeploymentLauncher (saved by Fritzing 0.9.2b)
circuit board: 8.46667cm x 5.64444cm
breadboards: 1

parts:
  U1 = Arduino Uno (Rev3)
  S1 = Toggle Switch [package=THT]
  S2 = Toggle Switch [package=THT]
  S3 = Pushbutton [package=THT]
  D3 = LED - 5mm [color="Green (555nm)" package="5 mm [THT]"]
  D1 = LED - 5mm [color="White (6500K)" package="5 mm [THT]"]
  D2 = LED - 5mm [color="Red (633nm)" package="5 mm [THT]"]

nets:
  N1: U1.D8, D2.anode
  N2: U1.D11_PWM/MOSI, D1.anode
  N3: U1.D12/MISO, D3.anode
  N4: U1.D2, S1.COM
  N5: U1.D4, S2.COM
  N6: U1.D7, S3.leg0
  N7: U1.GND, S1.L2, S2.L2, S3.leg1, D3.cathode, D1.cathode, D2.cathode
